# Fritzing sketch Cooling Fan Controller (saved by Fritzing 1.0.4)
stripboards: 1

parts:
  IC1 = Voltage Regulator [package=78xxl]
  DHT11 = DHT11 Humitidy and Temperature Sensor (3 pins)
  J4 = Camdenboss CTB0158-2 [part_number=CTB0158-2 package=THT]
  V_Battery = DC Power [voltage=12V internal_resistance=0.1Ω]
  Q1 = Basic FET N-Channel [part_number=IRLZ34N package="TO220 [THT]"]
  M1 = DC Motor [voltage_(max)=12V voltage_(min)=3V]
  M2 = DC Motor [voltage_(max)=12V voltage_(min)=3V]
  JP1 = Header 2 [package=molex-1x2_lock]
  JP2 = Header 2 [package=molex-1x2_lock]
  R2 = Resistor [tolerance=±5% resistance=10k power=0.25W package=THT]
  D1 = Rectifier Diode 800mil [part_number=1N4001 package="800 mil [THT]"]
  R1 = Resistor [tolerance=±5% power=0.25W resistance=220 package=THT]
  J3 = Camdenboss CTB0158-3 [part_number=CTB0158-3 package=THT]
  R3 = Resistor [tolerance=±5% power=0.25W resistance=10k package=THT]
  R4 = Resistor [tolerance=±5% power=0.25W resistance=10k package=THT]
  DS1 = DS18B20 1-Wire Temperature Sensor [part_number=DS18B20]
  WeMos_D1_Mini1 = WeMos D1 Mini

nets:
  GND: IC1.GND, DHT11.Gnd, J4.pin1, Q1.source, R2.Pin_0, J3.pin1, WeMos_D1_Mini1.G
  12V: IC1.IN, J4.pin2, M1.pin_1, M2.pin_1, JP1.1, JP2.1, D1.cathode
  5V: IC1.OUT, DHT11.Plus, J3.pin3, R3.Pin_1, R4.Pin_0, WeMos_D1_Mini1.5V
  N1: DHT11.Signal, R3.Pin_0, WeMos_D1_Mini1.D7
  N2: J4.terminal_1, V_Battery.V+
  N3: J4.terminal_2, V_Battery.V-
  N4: Q1.gate, R2.Pin_1, R1.Pin_0
  N5: Q1.drain, M1.pin_2, M2.pin_2, JP1.2, JP2.2, D1.anode
  N6: R1.Pin_1, WeMos_D1_Mini1.D2
  N7: J3.pin2, R4.Pin_1, DS1.DQ, WeMos_D1_Mini1.D5
  N8: J3.terminal_1, DS1.GND
  N9: J3.terminal_3, DS1.VDD

notes:
  12V to 5V Buck Converter
  Ambient Temperature Sensor
  Charger Temperature Sensor
  Fan Speed Driver
  The Brain

custom parts:
  DHT11 Humitidy and Temperature Sensor (3 pins): DHT11 Humidity and Temperature Sensor (3 pins).
  Rectifier Diode 800mil: A standard rectifier diode streched to 800mil
